// Digital circuit circuit.dig as structural Verilog
module circuit (
  input  X1,
  input  X0,
  input  CLK,
  output Verd,
  output Vermell,
  output Groc,
  output Blau
);

  wire and_1_out, and_2_out, and_3_out, and_4_out, and_5_out, and_6_out, and_7_out, and_8_out, and_9_out,
       and_10_out, and_11_out, and_12_out, and_13_out, D0_nq, D0_q, D1_nq, D1_q, D2_nq, D2_q, not_1_out,
       not_2_out, or_1_out, or_6_out;

  not not_1 (not_1_out, X1);
  not not_2 (not_2_out, X0);
  D_FF D2 (.D(X1), .C(CLK), .Q(D2_q), .nQ(D2_nq));
  D_FF D1 (.D(or_1_out), .C(CLK), .Q(D1_q), .nQ(D1_nq));
  D_FF D0 (.D(or_6_out), .C(CLK), .Q(D0_q), .nQ(D0_nq));
  and and_1 (and_1_out, D2_q, D0_q);
  and and_2 (and_2_out, D2_nq, D1_nq, D0_nq);
  and and_3 (and_3_out, D2_nq, D1_nq, D0_q);
  and and_4 (and_4_out, D2_nq, D1_q, D0_nq);
  and and_5 (and_5_out, D1_q, D0_q);
  and and_6 (and_6_out, D1_q, D0_nq, not_1_out, not_2_out);
  and and_7 (and_7_out, D2_nq, D1_nq, X0);
  and and_8 (and_8_out, D2_nq, D1_nq, D0_q, not_1_out);
  and and_9 (and_9_out, D1_q, D0_nq);
  and and_10 (and_10_out, D2_nq, D0_nq, not_1_out, not_2_out);
  and and_11 (and_11_out, D2_nq, D1_nq, D0_q, X0);
  and and_12 (and_12_out, D2_nq, X1);
  and and_13 (and_13_out, D2_q, D1_nq, D0_nq, X1);
  or or_1 (or_1_out, and_6_out, and_7_out, and_8_out);
  or or_2 (Verd, and_1_out, and_2_out);
  or or_3 (Vermell, and_1_out, and_3_out);
  or or_4 (Groc, and_1_out, and_4_out);
  or or_5 (Blau, and_1_out, and_5_out);
  or or_6 (or_6_out, and_9_out, and_10_out, and_11_out, and_12_out, and_13_out);

  // Notes on the sheet:
  //   D1
  //   D0
endmodule
