// Digital circuit solucio.dig as structural Verilog
module solucio (
  input  X1,
  input  X0,
  input  clk,
  output VERD,
  output VERMELL,
  output GROC,
  output BLAU
);

  circuit circuit_1 (.X1(X1), .X0(X0), .CLK(clk), .Verd(VERD), .Vermell(VERMELL), .Groc(GROC), .Blau(BLAU));
  LED LED_VERD (.in(VERD));
  LED LED_VERMELL (.in(VERMELL));
  LED LED_GROC (.in(GROC));
  LED LED_BLAU (.in(BLAU));
endmodule
